// Digital circuit hardware.dig as structural Verilog
module hardware (
  input  clk,
  input  in_2,
  input  in_3
);

  wire AluD, and_1_out, control_1_jreg, control_1_rreg, Halt, HiD, Jmp, jumpdecider_1_djmp, LoD, MemD,
       not_1_out, Phase_out, rs_ff_1_nq, rs_ff_1_q, RTD, RTW, Un_Halt_out;
  wire [3:0] alu_1_fl, AluOp, JT, RA, RT;
  wire [7:0] addrcalc_1_p1;
  wire [15:0] addrcalc_1_p2, addrcalc_1_p3, driver_1_out, InstrReg_q, jumpcalc_1_npc, multiplexer_1_out,
       PC_out, ramdualport_1_d, registerfile_1_da;

  Button Un_Halt (.out(Un_Halt_out));
  RS_FF rs_ff_1 (.S(Halt), .C(clk), .R(Un_Halt_out), .Q(rs_ff_1_q), .nQ(rs_ff_1_nq));
  and and_1 (and_1_out, rs_ff_1_nq, clk);
  LED Halted (.in(rs_ff_1_q));
  LED Running (.in(and_1_out));
  Counter Phase (.en(1'b1), .C(and_1_out), .clr(1'b0), .out(Phase_out));  // open: ovf
  not not_1 (not_1_out, Phase_out);
  CounterPreset #(.Bits(16)) PC (
    .en(not_1_out), .C(and_1_out), .dir(in_2), .in(jumpcalc_1_npc), .ld(jumpdecider_1_djmp), .clr(in_3),
    .out(PC_out));  // open: ovf
  // addrCalc addrcalc_1: pin names not known; wires that end beside it: addrcalc_1_p1, addrcalc_1_p2, addrcalc_1_p3
  Multiplexer #(.Bits(16)) multiplexer_1 (
    .sel(Phase_out), .in_0(PC_out), .in_1(addrcalc_1_p3), .out(multiplexer_1_out));
  RAMDualPort #(.AddrBits(16), .isProgramMemory("true"), .Bits(16)) ramdualport_1 (
    .A(multiplexer_1_out), .Din(driver_1_out), .str(RTD), .C(and_1_out), .ld(1'b1), .D(ramdualport_1_d));
  assign driver_1_out = MemD ? ramdualport_1_d : 16'bz;  // Driver driver_1
  Register #(.Bits(16)) InstrReg (.D(ramdualport_1_d), .C(and_1_out), .en(not_1_out), .Q(InstrReg_q));
  RegisterFile #(.AddrBits(4), .Bits(16)) registerfile_1 (
    .Din(driver_1_out), .we(RTW), .Rw(RT), .C(and_1_out), .Ra(RT), .Rb(RA), .Da(registerfile_1_da),
    .Db(addrcalc_1_p2));
  // Probe on InstrReg_q
  assign driver_1_out = RTD ? registerfile_1_da : 16'bz;  // Driver driver_2
  control control_1 (
    .Instr(InstrReg_q), .En(Phase_out), .RT(RT), .RTW(RTW), .RA(RA), .AluOp(AluOp), .AluD(AluD),
    .Imm(addrcalc_1_p1), .LoD(LoD), .HiD(HiD), .Jmp(Jmp), .JT(JT), .Halt(Halt), .JReg(control_1_jreg),
    .RReg(control_1_rreg), .MemD(MemD), .RTD(RTD));  // open: WMem, WPC, SPA, MSP, SPD, DtoPC
  alu alu_1 (
    .Op(AluOp), .TData(registerfile_1_da), .AData(addrcalc_1_p2), .DO(AluD), .Clk(and_1_out),
    .RData(driver_1_out), .Fl(alu_1_fl));
  // Probe on addrcalc_1_p1
  overwriter overwriter_1 (.Data(addrcalc_1_p1), .Lo(LoD), .Hi(HiD), .Val(registerfile_1_da), .ValU(driver_1_out));
  jumpCalc jumpcalc_1 (
    .PC(PC_out), .Imm(addrcalc_1_p1), .Reg(addrcalc_1_p2), .JReg(control_1_jreg), .RRel(control_1_rreg),
    .nPC(jumpcalc_1_npc));
  jumpDecider jumpdecider_1 (.Jmp(Jmp), .JT(JT), .Fl(alu_1_fl), .DJmp(jumpdecider_1_djmp));
  LED led_1 (.in(alu_1_fl[0]));
  LED led_2 (.in(alu_1_fl[1]));
  LED led_3 (.in(alu_1_fl[2]));
  LED led_4 (.in(alu_1_fl[3]));
  // Probe on PC_out
  // Probe on driver_1_out

  // Notes on the sheet:
  //   clk: Hz: 20
  //   Imm
  //   PC
  //   Data
  //   fN
  //   fZ
  //   fC
  //   fO
endmodule
